// Logisim project relogio.circ as structural Verilog
module main (
);

  contador_completo contador_completo_1 ();  // open: PRESET, CLK, VCC, in_1, in_2, in_3, in_4, in_5, in_6, in_7, in_8, in_9, in_10, in_11, in_12, in_13, in_14, in_15, in_16, in_17, in_18, in_19, in_20, in_21, in_22, in_23, in_24
endmodule

module contador4bits (
  input  PRESET,
  input  CLK,
  input  VCC,
  output Q1,
  output Q2,
  output Q3,
  output Q4,
  output SOUT
);

  wire fliflopjk_1_out_7, fliflopjk_2_out_7, fliflopjk_3_out_7;

  and and_1 (SOUT, Q4, fliflopjk_3_out_7, Q2, fliflopjk_1_out_7);
  fliflopjk fliflopjk_1 (
    .PRESET(PRESET), .J(VCC), .CLK(CLK), .K(VCC), .CLEAR(SOUT), .out_6(Q1), .out_7(fliflopjk_1_out_7));
  fliflopjk fliflopjk_2 (
    .PRESET(PRESET), .J(VCC), .CLK(fliflopjk_1_out_7), .K(VCC), .CLEAR(SOUT), .out_6(Q2),
    .out_7(fliflopjk_2_out_7));
  fliflopjk fliflopjk_3 (
    .PRESET(PRESET), .J(VCC), .CLK(fliflopjk_2_out_7), .K(VCC), .CLEAR(SOUT), .out_6(Q3),
    .out_7(fliflopjk_3_out_7));
  fliflopjk fliflopjk_4 (
    .PRESET(PRESET), .J(VCC), .CLK(fliflopjk_3_out_7), .K(VCC), .CLEAR(SOUT), .out_6(Q4));  // open: out_7
endmodule

module fliflopjk (
  input  PRESET,
  input  J,
  input  CLK,
  input  K,
  input  CLEAR,
  output out_6,
  output out_7
);

  wire nand_1_out, nand_2_out, nand_3_out, nand_4_out, nand_5_out, nand_6_out, not_1_out, not_2_out,
       not_3_out, or_1_out;

  or or_1 (or_1_out, PRESET, CLEAR);
  not not_1 (not_1_out, CLK);
  not not_2 (not_2_out, or_1_out);
  nand nand_1 (nand_1_out, out_7, J, not_1_out);
  nand nand_2 (nand_2_out, not_1_out, K, out_6);
  nand nand_3 (nand_3_out, 1'b1, nand_1_out, nand_4_out);
  not not_3 (not_3_out, not_1_out);
  nand nand_4 (nand_4_out, nand_3_out, nand_2_out, not_2_out);
  nand nand_5 (nand_5_out, not_2_out, nand_3_out, not_3_out);
  nand nand_6 (nand_6_out, not_3_out, nand_4_out, 1'b1);
  nand nand_7 (out_6, 1'b1, nand_5_out, out_7);
  nand nand_8 (out_7, out_6, nand_6_out, not_2_out);
endmodule

module contador_completo (
  input  in_1,
  input  in_2,
  input  in_3,
  input  in_4,
  input  in_5,
  input  in_6,
  input  in_7,
  input  in_8,
  input  in_9,
  input  in_10,
  input  in_11,
  input  in_12,
  input  in_13,
  input  in_14,
  input  in_15,
  input  in_16,
  input  in_17,
  input  in_18,
  input  in_19,
  input  in_20,
  input  in_21,
  input  in_22,
  input  in_23,
  input  in_24,
  input  PRESET,
  input  CLK,
  input  VCC
);

  wire contador4bits_1_sout, contador4bits_2_sout, contador4bits_3_sout, contador4bits_4_sout,
       contador4bits_5_p8;

  contador4bits contador4bits_1 (
    .SOUT(contador4bits_1_sout), .Q1(in_1), .Q2(in_2), .Q3(in_3), .Q4(in_4), .CLK(CLK), .PRESET(PRESET),
    .VCC(VCC));
  contador4bits contador4bits_2 (
    .SOUT(contador4bits_2_sout), .Q1(in_5), .Q2(in_6), .Q3(in_7), .Q4(in_8), .CLK(contador4bits_1_sout),
    .PRESET(PRESET), .VCC(VCC));
  contador4bits contador4bits_3 (
    .SOUT(contador4bits_3_sout), .Q1(in_9), .Q2(in_10), .Q3(in_11), .Q4(in_12), .CLK(contador4bits_2_sout),
    .PRESET(PRESET), .VCC(VCC));
  contador4bits contador4bits_4 (
    .SOUT(contador4bits_4_sout), .Q1(in_13), .Q2(in_14), .Q3(in_15), .Q4(in_16), .CLK(contador4bits_3_sout),
    .PRESET(PRESET), .VCC(VCC));
  // contador4bits contador4bits_5: pin names not known; wires that end beside it: in_17, PRESET, contador4bits_4_sout, VCC, in_18, in_19, in_20, contador4bits_5_p8
  contador4bits contador4bits_6 (
    .Q1(in_21), .Q2(in_22), .Q3(in_23), .Q4(in_24), .CLK(contador4bits_5_p8), .PRESET(PRESET), .VCC(VCC));  // open: SOUT
endmodule
